// Logisim project Acumulador A.circ as structural Verilog: 1 circuit, main circuit main
module main (
  input  Reset,
  input  Enable_Clock,
  input  [3:0] Input,
  input  Enable_Acumulador
);

  wire and_1_out, and_2_out, and_3_out, and_4_out, and_5_out, clock_1_out, FF_1_q, FF_1_qn, FF_2_q, FF_2_qn,
       FF_3_q, FF_3_qn, FF_4_q, FF_4_qn, not_1_out;

  Clock clock_1 (.out(clock_1_out));
  not not_1 (not_1_out, Reset);
  and and_1 (and_1_out, Enable_Clock, clock_1_out);
  D_Flip_Flop #(.Pre_Clr_Positions("BELOW_ABOVE")) FF_1 (
    .clk(and_1_out), .D(Input[0]), .Q(FF_1_q), .Qn(FF_1_qn), .reset(not_1_out));  // open: preset
  D_Flip_Flop #(.Pre_Clr_Positions("BELOW_ABOVE")) FF_2 (
    .clk(and_1_out), .D(Input[1]), .Q(FF_2_q), .Qn(FF_2_qn), .reset(not_1_out));  // open: preset
  D_Flip_Flop #(.Pre_Clr_Positions("BELOW_ABOVE")) FF_3 (
    .clk(and_1_out), .D(Input[2]), .Q(FF_3_q), .Qn(FF_3_qn), .reset(not_1_out));  // open: preset
  LED S1 (.in(FF_1_q));
  LED S2 (.in(FF_2_q));
  LED S3 (.in(FF_3_q));
  LED S4__MSB (.in(FF_4_q));
  D_Flip_Flop #(.Pre_Clr_Positions("BELOW_ABOVE")) FF_4 (
    .clk(and_1_out), .D(Input[3]), .Q(FF_4_q), .Qn(FF_4_qn), .reset(not_1_out));  // open: preset
  and and_2 (and_2_out, ~FF_4_qn, Enable_Acumulador);  // AND_Gate
  and and_3 (and_3_out, ~FF_3_qn, Enable_Acumulador);  // AND_Gate
  and and_4 (and_4_out, ~FF_2_qn, Enable_Acumulador);  // AND_Gate
  LED S4__MSB_2 (.in(and_2_out));
  LED S3_2 (.in(and_3_out));
  LED S2_2 (.in(and_4_out));
  LED S1_2 (.in(and_5_out));
  and and_5 (and_5_out, ~FF_1_qn, Enable_Acumulador);  // AND_Gate
endmodule
