// Logisim project VSM.circ as structural Verilog
// Acum A
module Acumulador_A (
  input  ClearA,
  input  Enable_Clock,
  input  in_3,
  input  A0,
  input  A1,
  input  A2,
  input  A3_MSB,
  input  Enable_Acumulador,
  output S0,
  output S1,
  output S2,
  output S3__MSB,
  output S0_2,
  output S1_2,
  output S2_2,
  output S3__MSB_2
);

  wire and_1_out, d_ff_1_qn, d_ff_2_qn, d_ff_3_qn, d_ff_4_qn;

  and and_1 (and_1_out, Enable_Clock, in_3);
  D_Flip_Flop d_ff_1 (.clk(and_1_out), .D(A0), .Q(S0), .Qn(d_ff_1_qn), .preset(ClearA));  // open: reset
  D_Flip_Flop d_ff_2 (.clk(and_1_out), .D(A1), .Q(S1), .Qn(d_ff_2_qn), .preset(ClearA));  // open: reset
  D_Flip_Flop d_ff_3 (.clk(and_1_out), .D(A2), .Q(S2), .Qn(d_ff_3_qn), .preset(ClearA));  // open: reset
  D_Flip_Flop d_ff_4 (.clk(and_1_out), .D(A3_MSB), .Q(S3__MSB), .Qn(d_ff_4_qn), .preset(ClearA));  // open: reset
  assign S0_2 = Enable_Acumulador ? ~d_ff_1_qn : 1'bz;  // Controlled_Inverter controlled_inverter_1
  assign S1_2 = Enable_Acumulador ? ~d_ff_2_qn : 1'bz;  // Controlled_Inverter controlled_inverter_2
  assign S2_2 = Enable_Acumulador ? ~d_ff_3_qn : 1'bz;  // Controlled_Inverter controlled_inverter_3
  assign S3__MSB_2 = Enable_Acumulador ? ~d_ff_4_qn : 1'bz;  // Controlled_Inverter controlled_inverter_4
endmodule

module Somador_Completo (
  input  A,
  input  B,
  input  Cin,
  output Cout,
  output Sum
);

  wire and_1_out, and_2_out, or_1_out, xor_1_out;

  and and_1 (and_1_out, A, B);
  or or_1 (or_1_out, A, B);
  xor xor_1 (xor_1_out, A, B);
  or or_2 (Cout, and_1_out, and_2_out);
  and and_2 (and_2_out, or_1_out, Cin);
  xor xor_2 (Sum, xor_1_out, Cin);
endmodule

// Bit Decoder
module Decodificador_bit_hexa (
  input  S3,
  input  S2,
  input  S1,
  input  S0,
  output A,
  output B,
  output C,
  output D,
  output E,
  output F,
  output G
);

  wire and_1_out, and_2_out, and_3_out, and_4_out, and_5_out, and_6_out, and_7_out, and_8_out, and_9_out,
       and_10_out, and_11_out, and_12_out, and_13_out, and_14_out, and_15_out, and_16_out, and_17_out,
       and_18_out, and_19_out, and_20_out, and_21_out, nor_1_out, nor_2_out, nor_3_out, or_1_out, or_2_out,
       or_3_out, or_4_out, or_5_out, or_6_out, or_7_out, or_8_out, or_9_out, or_10_out, or_11_out, xor_1_out,
       xor_2_out, xor_3_out;

  or or_1 (or_1_out, ~S0, ~S2, S3);  // OR_Gate
  or or_2 (or_2_out, S0, ~S2);  // OR_Gate
  or or_3 (or_3_out, S1, ~S2);  // OR_Gate
  or or_4 (or_4_out, ~S2, S3);  // OR_Gate
  and and_1 (and_1_out, S0, ~S3);  // AND_Gate
  or or_5 (or_5_out, ~S0, ~S3);  // OR_Gate
  or or_6 (or_6_out, S1, S2);
  or or_7 (or_7_out, S1, ~S2);  // OR_Gate
  and and_2 (and_2_out, ~S1, S3);  // AND_Gate
  and and_3 (and_3_out, S0, S1);
  and and_4 (and_4_out, or_1_out, S1);
  and and_5 (and_5_out, or_2_out, S3);
  and and_6 (and_6_out, ~S1, S2, ~S3);  // AND_Gate
  nor nor_1 (nor_1_out, S0, S1);
  and and_7 (and_7_out, or_3_out, S3);
  nor nor_2 (nor_2_out, S1, S3);
  or or_8 (or_8_out, nor_2_out, ~S0);  // OR_Gate
  and and_8 (and_8_out, or_4_out, ~S0);  // AND_Gate
  or or_9 (or_9_out, and_1_out, S1);
  and and_9 (and_9_out, ~S0, ~S1, ~S3);  // AND_Gate
  xor xor_1 (xor_1_out, S1, S3);
  and and_10 (and_10_out, xor_1_out, S0);
  and and_11 (and_11_out, or_5_out, ~S2);  // AND_Gate
  and and_12 (and_12_out, or_6_out, S3);
  and and_13 (and_13_out, or_7_out, ~S0);  // AND_Gate
  xor xor_2 (xor_2_out, S0, S1);
  and and_14 (and_14_out, xor_2_out, S2);
  or or_10 (or_10_out, and_3_out, nor_3_out);
  nor nor_3 (nor_3_out, S0, S3);
  and and_15 (and_15_out, ~S1, ~S2);  // AND_Gate
  or or_11 (or_11_out, ~S1, ~S2);  // OR_Gate
  and and_16 (and_16_out, or_11_out, S0);
  xor xor_3 (xor_3_out, S2, S3);
  or or_12 (A, and_4_out, and_5_out, and_6_out);
  or or_13 (B, nor_1_out, and_7_out, and_17_out);
  and and_17 (and_17_out, or_8_out, S2);
  or or_14 (C, and_8_out, and_18_out, and_19_out, and_20_out);
  and and_18 (and_18_out, or_9_out, S2);
  and and_19 (and_19_out, S1, ~S3);  // AND_Gate
  and and_20 (and_20_out, ~S1, ~S2, S3);  // AND_Gate
  or or_15 (D, and_9_out, and_10_out, and_11_out);
  or or_16 (E, and_12_out, and_13_out);
  or or_17 (F, and_2_out, and_14_out, and_21_out);
  and and_21 (and_21_out, or_10_out, ~S2);  // AND_Gate
  or or_18 (G, and_15_out, and_16_out, xor_3_out);
endmodule

module ULA (
  input  EnableAlu,
  input  B3_MSB,
  input  B2,
  input  B1,
  input  B0,
  input  A3_MSB,
  input  A2,
  input  A1,
  input  A0,
  input  AddSub,
  output Cout,
  output S3,
  output S2,
  output S1,
  output S0
);

  wire multiplexer_1_out, multiplexer_2_out, multiplexer_3_out, multiplexer_4_out, multiplexer_5_out,
       not_1_out, not_2_out, not_3_out, not_4_out, somador_completo_1_sum, somador_completo_2_cout,
       somador_completo_2_sum, somador_completo_3_cout, somador_completo_3_sum, somador_completo_4_cout,
       somador_completo_4_sum;

  Multiplexer #(.enable("false")) multiplexer_1 (.in0(A3_MSB), .in1(not_1_out), .out(multiplexer_1_out), .sel(AddSub));
  not not_1 (not_1_out, A3_MSB);
  Multiplexer #(.enable("false")) multiplexer_2 (.in0(A2), .in1(not_2_out), .out(multiplexer_2_out), .sel(AddSub));
  not not_2 (not_2_out, A2);
  Multiplexer #(.enable("false")) multiplexer_3 (.in0(A1), .in1(not_3_out), .out(multiplexer_3_out), .sel(AddSub));
  not not_3 (not_3_out, A1);
  Multiplexer #(.enable("false")) multiplexer_4 (.in0(A0), .in1(not_4_out), .out(multiplexer_4_out), .sel(AddSub));
  not not_4 (not_4_out, A0);
  Multiplexer #(.enable("false")) multiplexer_5 (.in0(1'b0), .in1(1'b1), .out(multiplexer_5_out), .sel(AddSub));
  Somador_Completo somador_completo_1 (
    .A(B3_MSB), .B(multiplexer_1_out), .Cin(somador_completo_2_cout), .Cout(Cout),
    .Sum(somador_completo_1_sum));
  Somador_Completo somador_completo_2 (
    .A(B2), .B(multiplexer_2_out), .Cin(somador_completo_3_cout), .Cout(somador_completo_2_cout),
    .Sum(somador_completo_2_sum));
  Somador_Completo somador_completo_3 (
    .A(B1), .B(multiplexer_3_out), .Cin(somador_completo_4_cout), .Cout(somador_completo_3_cout),
    .Sum(somador_completo_3_sum));
  Somador_Completo somador_completo_4 (
    .A(B0), .B(multiplexer_4_out), .Cin(multiplexer_5_out), .Cout(somador_completo_4_cout),
    .Sum(somador_completo_4_sum));
  assign S3 = EnableAlu ? somador_completo_1_sum : 1'bz;  // Controlled_Buffer controlled_buffer_1
  assign S2 = EnableAlu ? somador_completo_2_sum : 1'bz;  // Controlled_Buffer controlled_buffer_2
  assign S1 = EnableAlu ? somador_completo_3_sum : 1'bz;  // Controlled_Buffer controlled_buffer_3
  assign S0 = EnableAlu ? somador_completo_4_sum : 1'bz;  // Controlled_Buffer controlled_buffer_4
endmodule

// Acum B
module Acumulador_B (
  input  ClearB,
  input  Enable_Clock,
  input  Clock,
  input  B0,
  input  B1,
  input  B2,
  input  B3_MSB,
  output S0,
  output S1,
  output S2,
  output S3__MSB
);

  wire and_1_out;

  and and_1 (and_1_out, Enable_Clock, Clock);
  D_Flip_Flop #(.Pre_Clr_Positions("BELOW_ABOVE")) FF_1 (
    .clk(and_1_out), .D(B0), .Q(S0), .reset(ClearB));  // open: Qn, preset
  D_Flip_Flop #(.Pre_Clr_Positions("BELOW_ABOVE")) FF_2 (
    .clk(and_1_out), .D(B1), .Q(S1), .reset(ClearB));  // open: Qn, preset
  D_Flip_Flop #(.Pre_Clr_Positions("BELOW_ABOVE")) FF_3 (
    .clk(and_1_out), .D(B2), .Q(S2), .reset(ClearB));  // open: Qn, preset
  D_Flip_Flop #(.Pre_Clr_Positions("BELOW_ABOVE")) FF_4 (
    .clk(and_1_out), .D(B3_MSB), .Q(S3__MSB), .reset(ClearB));  // open: Qn, preset
endmodule

module Complete_ULA (
  input  LatchA,
  input  LatchB,
  input  Clear,
  input  EnableULA,
  input  [3:0] B,
  input  [3:0] A,
  input  EnableA,
  input  AddSub,
  output Cout
);

  wire acumulador_a_1_s0_2, acumulador_a_1_s1_2, acumulador_a_1_s2_2, acumulador_a_1_s3__msb_2,
       acumulador_b_1_s0, acumulador_b_1_s1, acumulador_b_1_s2, acumulador_b_1_s3__msb, Clock_out,
       decodificador_bit_hexa_1_a, decodificador_bit_hexa_1_b, decodificador_bit_hexa_1_c,
       decodificador_bit_hexa_1_d, decodificador_bit_hexa_1_e, decodificador_bit_hexa_1_f,
       decodificador_bit_hexa_1_g, ula_1_s0, ula_1_s1, ula_1_s2, ula_1_s3;

  Clock Clock (.out(Clock_out));
  Acumulador_B acumulador_b_1 (
    .ClearB(Clear), .Enable_Clock(LatchB), .Clock(Clock_out), .B0(B[3]), .B1(B[2]), .B2(B[1]), .B3_MSB(B[0]),
    .S0(acumulador_b_1_s0), .S1(acumulador_b_1_s1), .S2(acumulador_b_1_s2), .S3__MSB(acumulador_b_1_s3__msb));
  Acumulador_A acumulador_a_1 (
    .ClearA(Clear), .Enable_Clock(LatchA), .in_3(Clock_out), .A0(A[3]), .A1(A[2]), .A2(A[1]), .A3_MSB(A[0]),
    .Enable_Acumulador(EnableA), .S0_2(acumulador_a_1_s0_2), .S1_2(acumulador_a_1_s1_2),
    .S2_2(acumulador_a_1_s2_2), .S3__MSB_2(acumulador_a_1_s3__msb_2));  // open: S0, S1, S2, S3__MSB
  ULA ula_1 (
    .B3_MSB(acumulador_b_1_s0), .B2(acumulador_b_1_s1), .B1(acumulador_b_1_s2), .B0(acumulador_b_1_s3__msb),
    .A3_MSB(acumulador_a_1_s0_2), .A2(acumulador_a_1_s1_2), .A1(acumulador_a_1_s2_2),
    .A0(acumulador_a_1_s3__msb_2), .AddSub(AddSub), .Cout(Cout), .EnableAlu(EnableULA), .S3(ula_1_s3),
    .S2(ula_1_s2), .S1(ula_1_s1), .S0(ula_1_s0));
  _7_Segment_Display u_7_segment_display_1 (
    .g(decodificador_bit_hexa_1_a), .f(decodificador_bit_hexa_1_b), .a(decodificador_bit_hexa_1_c),
    .b(decodificador_bit_hexa_1_d), .e(decodificador_bit_hexa_1_e), .d(decodificador_bit_hexa_1_f),
    .c(decodificador_bit_hexa_1_g));  // open: dp
  Decodificador_bit_hexa decodificador_bit_hexa_1 (
    .S3(ula_1_s3), .S2(ula_1_s2), .S1(ula_1_s1), .S0(ula_1_s0), .A(decodificador_bit_hexa_1_a),
    .B(decodificador_bit_hexa_1_b), .C(decodificador_bit_hexa_1_c), .D(decodificador_bit_hexa_1_d),
    .E(decodificador_bit_hexa_1_e), .F(decodificador_bit_hexa_1_f), .G(decodificador_bit_hexa_1_g));
endmodule
